# Fritzing sketch L06_Encoder (saved by Fritzing 0.9.4)
breadboards: 1

parts:
  Part1 = 12 NeoPixel Ring [part_number=1643]
  Teensy_3_1 = Teensy 3.1
  WS2812B1 = WS2812B [package="DIP (Dual Inline) [THT]"]
  WS2812B2 = WS2812B [package="DIP (Dual Inline) [THT]"]
  WS2812B3 = WS2812B [package="DIP (Dual Inline) [THT]"]
  WS2812B4 = WS2812B [package="DIP (Dual Inline) [THT]"]
  RG_encoder1 = SprkFn RG Encoder [package="DIP (Dual Inline) [THT]"]
  C1 = Capacitor [package=cap-pth-small2]
  C2 = Capacitor [package=cap-pth-small2]

nets:
  N1: Part1.IN, WS2812B4.DO
  5V: Part1.VDD, Teensy_3_1.3V3, WS2812B2.5V, WS2812B3.5V, WS2812B4.5V
  GND: Part1.GND, Teensy_3_1.GND, WS2812B1.GND, WS2812B2.GND, WS2812B3.GND, WS2812B4.GND, RG_encoder1.GND, RG_encoder1.B, C1.1, C2.2
  N2: Teensy_3_1.A3/D17, WS2812B1.DI
  N3: Teensy_3_1.A9/D23, RG_encoder1.SW
  N4: WS2812B1.DO, WS2812B2.DI
  N5: WS2812B2.DO, WS2812B3.DI
  N6: WS2812B3.DO, WS2812B4.DI
  N7: RG_encoder1.A, C2.1
  N8: RG_encoder1.C, C1.2

custom parts:
  12 NeoPixel Ring: 12 ultra bright smart LED NeoPixels are arranged in a circle with 1.5" (37mm) outer diameter. The rings are 'chainable' - connect the output pin of one to the input pin of another. Use only one microcontroller pin to control as many as you can chain together! Each LED is addressable as the driver chip is inside the LED. Each one has ~18mA constant current drive so the color will be very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
  WS2812B: Adafruit NeoPixel Breakout
  SprkFn RG Encoder: SparkFun RG Rotary Encoder
